// Logisim project 555_timer_reconstructed.circ as structural Verilog: 1 circuit, main circuit main
module main (
);


  // Notes on the sheet:
  //   555 TIMER PCB — reconstructed from Eagle board XML
  //   This is a netlist reference only; analog 555 operation is not simulated.
  //   SUPPLY / CONNECTOR JP1
  //   JP1 pin 1: GND (board net JP1_GND)
  //   JP1 pin 4: VCC (board net JP1_VCC)
  //   LM555 (U1) — PCB contact-reference connections
  //   Pin 1 GND  → JP1_GND
  //   Pin 2 TRIG → U1_TR
  //   Pin 3 OUT  → U1_OUT → PIEZO1 pin 1
  //   Pin 4 RESET → JP1_VCC
  //   Pin 5 CTRL  → U1_TR (same net as pin 2 per PCB XML)
  //   Pin 6 THRESH → U1_THR → C8 pin 2
  //   Pin 7 DISCH → U1_DIS → R3 pin 2, RPOT1 pin 1
  //   Pin 8 VCC   → U1_V+ → R3 pin 1
  //   OTHER COMPONENTS / NETS
  //   C7 10 nF: pin 1 → GND; pin 2 → U1_TR
  //   C8 100 nF: pin 1 → GND; pin 2 → U1_THR
  //   RPOT1 100 kΩ: pin 1 → U1_DIS; pin 2 → U1_TR
  //   R3 1 kΩ: pin 1 → U1_V+; pin 2 → U1_DIS
  //   PIEZO1: pin 1 → U1_OUT; pin 2 → GND
  //   CHECK BEFORE BUILDING
  //   The board file contains PCB nets, not the original schematic.
  //   Pin 2 and pin 5 are joined; this is unusual. Verify against the
  //   intended 555 circuit before powering it. Component pad numbering
  //   is taken from the uploaded board XML, not independently verified.
endmodule
